# Fritzing sketch temperature_sensor (saved by Fritzing 0.9.1b)
circuit board: 3.38812cm x 4.50012cm
breadboards: 1

parts:
  JP1 = Header 3 [package=screwterminal-3.5mm-3_lock.007s]
  J1 = shrouded pin header, 26 pins [form="♂ (shrouded male)"]
  R1 = Resistor [tolerance=±5% resistance=4.7k package=THT]
  JP2 = Header 3 [package=screwterminal-3.5mm-3_lock.007s]
  JP3 = Header 3 [package=screwterminal-3.5mm-3_lock.007s]

nets:
  N1: JP1.1, J1.pin4, R1.Pin_0, JP2.1, JP3.1
  N2: JP1.2, J1.pin1, R1.Pin_1, JP2.2, JP3.2
  N3: JP1.3, J1.pin24, JP2.3, JP3.3
